// Logisim project 6551071049_LAB1_b1trang4.circ as structural Verilog: 1 circuit, main circuit main
module main (
  input  D3,
  input  A1,
  input  A3,
  output Y0,
  output Y1,
  output Y2,
  output Y3,
  output Y4,
  output Y5,
  output Y6,
  output Y7
);

  wire not_1_out, not_2_out, not_3_out;

  not not_1 (not_1_out, D3);
  not not_2 (not_2_out, A1);
  not not_3 (not_3_out, A1);
  and and_1 (Y0, not_3_out, not_2_out, not_1_out);
  and and_2 (Y1, A1, not_2_out, not_1_out);
  and and_3 (Y2, not_3_out, A1, not_1_out);
  and and_4 (Y3, A1, A1, not_1_out);
  and and_5 (Y4, not_3_out, not_2_out, D3);
  and and_6 (Y5, A1, not_2_out, D3);
  and and_7 (Y6, not_3_out, A1, D3);
  and and_8 (Y7, A1, A1, D3);

  assign A3 = A1;

  // Notes on the sheet:
  //   Nguyễn Hữu Khoa_6551071049
endmodule
